# Fritzing sketch uno2tap (saved by Fritzing 0.9.3b)
circuit board: 8.46667cm x 5.64444cm
breadboards: 1

parts:
  Componente1 = Arduino Uno (Rev3)
  R1 = Resistor [tolerance=±5% resistance=100k package=THT]

nets:
  N1: Componente1.GND, R1.Pin_1
  N2: Componente1.D6_PWM, R1.Pin_0

notes:
  Cable from C64 to cassette (see https://www.c64-wiki.com/wiki/Cassette_Port for details)
  Motor
  Read
  Write
  Sense
  GND
  100k resistor
